// Logisim project circuitoVLIW.circ as structural Verilog: 6 circuits, main circuit main
module main (
);

  wire ABrJump, and_1_out, and_2_out, brzr, clock_1_out, High, IBrJump, jump, mov, or_1_out, RBrJump,
       reset_out, WELSM, WEmem, WEULA1, WEULA2;
  wire [1:0] multiplexer_3_out, multiplexer_4_out;
  wire [2:0] opULA1, opULA2;
  wire [7:0] adder_1_out, BBrJump, bit_extender_1_out, move_1_movh, move_1_movl, multiplexer_1_out,
       multiplexer_2_out, multiplexer_5_out, multiplexer_6_out, ram_1_dout, regbank_1_brjump,
       regbank_1_ldstmov, regbank_1_ldstmov2, regbank_1_ula, regbank_1_ula12, regbank_1_ula21,
       regbank_1_ula22, register_1_q, ula_1_d, ula_2_d;
  wire [31:0] rom_1_data;

  and and_1 (and_1_out, ABrJump, brzr);
  or or_1 (or_1_out, and_1_out, jump);
  Multiplexer #(.width(8)) multiplexer_1 (.in0(adder_1_out), .in1(BBrJump), .out(multiplexer_1_out), .sel(or_1_out));
  Clock clock_1 (.out(clock_1_out));
  Register register_1 (.D(multiplexer_1_out), .en(1'b1), .clk(clock_1_out), .Q(register_1_q), .clr(reset_out));
  Button reset (.out(reset_out));
  Multiplexer #(.width(8)) multiplexer_2 (
    .in0(8'h1), .in1(bit_extender_1_out), .out(multiplexer_2_out), .sel(and_2_out));
  and and_2 (and_2_out, IBrJump, ABrJump);
  ROM #(.dataWidth(32)) rom_1 (.addr(register_1_q), .data(rom_1_data));
  Adder adder_1 (.a(register_1_q), .b(multiplexer_2_out), .out(adder_1_out));  // open: cin, cout
  assign bit_extender_1_out = {{4{rom_1_data[19]}}, rom_1_data[19:16]};  // Bit_Extender bit_extender_1
  Multiplexer #(.width(2)) multiplexer_3 (.in0(rom_1_data[27:26]), .in1(2'b00), .out(multiplexer_3_out), .sel(mov));
  Multiplexer #(.width(2)) multiplexer_4 (.in0(rom_1_data[19:18]), .in1(2'b00), .out(multiplexer_4_out), .sel(IBrJump));
  RegBank regbank_1 (
    .W0(multiplexer_6_out), .W1(ula_1_d), .W2(ula_2_d), .WLdStMov(WELSM), .WULA(WEULA1), .WULA2(WEULA2),
    .R(reset_out), .R6(rom_1_data[3:2]), .R7(rom_1_data[1:0]), .R0(multiplexer_3_out),
    .R1(rom_1_data[25:24]), .R2(multiplexer_4_out), .R3(rom_1_data[17:16]), .R4(rom_1_data[11:10]),
    .R5(rom_1_data[9:8]), .ULA21(regbank_1_ula21), .ULA22(regbank_1_ula22), .LdStMov(regbank_1_ldstmov),
    .LdStMov2(regbank_1_ldstmov2), .BrJump(regbank_1_brjump), .BrJump2(BBrJump), .ULA(regbank_1_ula),
    .ULA12(regbank_1_ula12));
  control control_1 (
    .LdStMov(rom_1_data[31:28]), .BrJump(rom_1_data[23:20]), .ULA1(rom_1_data[15:12]),
    .ULA2(rom_1_data[7:4]), .High(High), .Move(mov), .WELdStMov(WELSM), .WEmem(WEmem), .brzr(brzr),
    .RBrJump(RBrJump), .jump(jump), .IBrJump(IBrJump), .WEULA1(WEULA1), .opULA1(opULA1), .WEULA2(WEULA2),
    .opoULA2(opULA2));
  move move_1 (.R0(regbank_1_ldstmov), .Imm(rom_1_data[27:24]), .movL(move_1_movl), .movH(move_1_movh));
  isZero iszero_1 (.in_1(regbank_1_brjump), .out_2(ABrJump));
  ULA ula_1 (.B(regbank_1_ula12), .A(regbank_1_ula), .ALUop(opULA1), .D(ula_1_d));
  ULA ula_2 (.B(regbank_1_ula22), .A(regbank_1_ula21), .ALUop(opULA2), .D(ula_2_d));
  Multiplexer #(.width(8)) multiplexer_5 (.in0(move_1_movl), .in1(move_1_movh), .out(multiplexer_5_out), .sel(High));
  RAM ram_1 (
    .addr(regbank_1_ldstmov), .we(WEmem), .oe(1'b1), .clk(clock_1_out), .din(regbank_1_ldstmov2),
    .dout(ram_1_dout));
  Multiplexer #(.width(8)) multiplexer_6 (
    .in0(ram_1_dout), .in1(multiplexer_5_out), .out(multiplexer_6_out), .sel(mov));

  // Notes on the sheet:
  //   contents of rom_1 (hex, n*v repeats v):
  //   61ffffff 54ffffff 46ffffff
endmodule

module RegBank (
  input  [1:0] R0,
  input  [1:0] R1,
  input  [1:0] R2,
  input  [1:0] R3,
  input  [1:0] R4,
  input  [1:0] R5,
  input  R,
  input  [7:0] W0,
  input  [7:0] W1,
  input  [7:0] W2,
  input  WLdStMov,
  input  WULA,
  input  WULA2,
  input  [1:0] R6,
  input  [1:0] R7,
  output [7:0] LdStMov,
  output [7:0] LdStMov2,
  output [7:0] BrJump,
  output [7:0] BrJump2,
  output [7:0] ULA,
  output [7:0] ULA12,
  output [7:0] ULA21,
  output [7:0] ULA22
);

  wire clock_1_out, demultiplexer_4_out0, demultiplexer_4_out1, demultiplexer_4_out2, demultiplexer_4_out3,
       demultiplexer_5_out0, demultiplexer_5_out1, demultiplexer_5_out2, demultiplexer_5_out3,
       demultiplexer_6_out0, demultiplexer_6_out1, demultiplexer_6_out2, demultiplexer_6_out3, or_5_out,
       or_6_out, or_7_out, or_8_out;
  wire [7:0] demultiplexer_1_out0, demultiplexer_1_out1, demultiplexer_1_out2, demultiplexer_1_out3,
       demultiplexer_2_out0, demultiplexer_2_out1, demultiplexer_2_out2, demultiplexer_2_out3,
       demultiplexer_3_out0, demultiplexer_3_out1, demultiplexer_3_out2, demultiplexer_3_out3, or_1_out,
       or_2_out, or_3_out, or_4_out, register_1_q, register_2_q, register_3_q, register_4_q;

  Demultiplexer #(.select(2), .width(8)) demultiplexer_1 (
    .out0(demultiplexer_1_out0), .out1(demultiplexer_1_out1), .out2(demultiplexer_1_out2),
    .out3(demultiplexer_1_out3), .in(W0), .sel(R0));
  Demultiplexer #(.select(2), .width(8)) demultiplexer_2 (
    .out0(demultiplexer_2_out0), .out1(demultiplexer_2_out1), .out2(demultiplexer_2_out2),
    .out3(demultiplexer_2_out3), .in(W1), .sel(R4));
  Demultiplexer #(.select(2), .width(8)) demultiplexer_3 (
    .out0(demultiplexer_3_out0), .out1(demultiplexer_3_out1), .out2(demultiplexer_3_out2),
    .out3(demultiplexer_3_out3), .in(W2), .sel(R6));
  assign or_1_out = demultiplexer_1_out0 | demultiplexer_2_out0 | demultiplexer_3_out0;  // OR_Gate or_1, 8 bits wide
  assign or_2_out = demultiplexer_1_out1 | demultiplexer_2_out1 | demultiplexer_3_out1;  // OR_Gate or_2, 8 bits wide
  assign or_3_out = demultiplexer_1_out2 | demultiplexer_2_out2 | demultiplexer_3_out2;  // OR_Gate or_3, 8 bits wide
  assign or_4_out = demultiplexer_1_out3 | demultiplexer_2_out3 | demultiplexer_3_out3;  // OR_Gate or_4, 8 bits wide
  Demultiplexer #(.select(2)) demultiplexer_4 (
    .out0(demultiplexer_4_out0), .out1(demultiplexer_4_out1), .out2(demultiplexer_4_out2),
    .out3(demultiplexer_4_out3), .in(WLdStMov), .sel(R0));
  Demultiplexer #(.select(2)) demultiplexer_5 (
    .out0(demultiplexer_5_out0), .out1(demultiplexer_5_out1), .out2(demultiplexer_5_out2),
    .out3(demultiplexer_5_out3), .in(WULA), .sel(R4));
  or or_5 (or_5_out, demultiplexer_4_out0, demultiplexer_5_out0, demultiplexer_6_out0);
  or or_6 (or_6_out, demultiplexer_4_out1, demultiplexer_5_out1, demultiplexer_6_out1);
  or or_7 (or_7_out, demultiplexer_4_out2, demultiplexer_5_out2, demultiplexer_6_out2);
  or or_8 (or_8_out, demultiplexer_4_out3, demultiplexer_5_out3, demultiplexer_6_out3);
  Demultiplexer #(.select(2)) demultiplexer_6 (
    .out0(demultiplexer_6_out0), .out1(demultiplexer_6_out1), .out2(demultiplexer_6_out2),
    .out3(demultiplexer_6_out3), .in(WULA2), .sel(R6));
  Register register_1 (.D(or_1_out), .en(or_5_out), .clk(clock_1_out), .Q(register_1_q), .clr(R));
  Register register_2 (.D(or_2_out), .en(or_6_out), .clk(clock_1_out), .Q(register_2_q), .clr(R));
  Register register_3 (.D(or_3_out), .en(or_7_out), .clk(clock_1_out), .Q(register_3_q), .clr(R));
  Register register_4 (.D(or_4_out), .en(or_8_out), .clk(clock_1_out), .Q(register_4_q), .clr(R));
  Clock clock_1 (.out(clock_1_out));
  Multiplexer #(.select(2), .width(8)) multiplexer_1 (
    .in0(register_1_q), .in1(register_2_q), .in2(register_3_q), .in3(register_4_q), .out(LdStMov), .sel(R0));
  Multiplexer #(.select(2), .width(8)) multiplexer_2 (
    .in0(register_1_q), .in1(register_2_q), .in2(register_3_q), .in3(register_4_q), .out(LdStMov2), .sel(R1));
  Multiplexer #(.select(2), .width(8)) multiplexer_3 (
    .in0(register_1_q), .in1(register_2_q), .in2(register_3_q), .in3(register_4_q), .out(BrJump), .sel(R2));
  Multiplexer #(.select(2), .width(8)) multiplexer_4 (
    .in0(register_1_q), .in1(register_2_q), .in2(register_3_q), .in3(register_4_q), .out(BrJump2), .sel(R3));
  Multiplexer #(.select(2), .width(8)) multiplexer_5 (
    .in0(register_1_q), .in1(register_2_q), .in2(register_3_q), .in3(register_4_q), .out(ULA), .sel(R4));
  Multiplexer #(.select(2), .width(8)) multiplexer_6 (
    .in0(register_1_q), .in1(register_2_q), .in2(register_3_q), .in3(register_4_q), .out(ULA12), .sel(R5));
  Multiplexer #(.select(2), .width(8)) multiplexer_7 (
    .in0(register_1_q), .in1(register_2_q), .in2(register_3_q), .in3(register_4_q), .out(ULA21), .sel(R6));
  Multiplexer #(.select(2), .width(8)) multiplexer_8 (
    .in0(register_1_q), .in1(register_2_q), .in2(register_3_q), .in3(register_4_q), .out(ULA22), .sel(R7));

  // Other names for the same wires on the sheet: LdStMov_t[1:0] = R0; ULA2[1:0] = R6; ULA_t[1:0] = R4
endmodule

module ULA (
  input  [7:0] A,
  input  [7:0] B,
  input  [2:0] ALUop,
  output [7:0] D
);

  wire [7:0] adder_1_out, not_1_out, or_1_out, shifter_1_out, shifter_2_out, subtractor_1_out;

  Adder adder_1 (.a(A), .b(B), .out(adder_1_out));  // open: cin, cout
  Subtractor subtractor_1 (.a(A), .b(B), .out(subtractor_1_out));  // open: bin, bout
  assign or_1_out = A | B;  // OR_Gate or_1, 8 bits wide
  assign not_1_out = ~A;  // NOT_Gate not_1, 8 bits wide
  Shifter shifter_1 (.in(A), .out(shifter_1_out));  // open: dist
  Shifter #(.shift("lr")) shifter_2 (.in(A), .out(shifter_2_out));  // open: dist
  Multiplexer #(.select(3), .width(8)) multiplexer_1 (
    .in0(adder_1_out), .in1(subtractor_1_out), .in3(or_1_out), .in4(not_1_out), .in5(shifter_1_out),
    .in6(shifter_2_out), .out(D), .sel(ALUop));  // open: in2, in7
endmodule

module isZero (
  input  [7:0] in_1,
  output out_2
);

  nor nor_1 (out_2, in_1[0], in_1[1], in_1[2], in_1[3], in_1[4], in_1[5], in_1[6], in_1[7]);
endmodule

module move (
  input  [7:0] R0,
  input  [3:0] Imm,
  output [7:0] movH,
  output [7:0] movL
);


  assign movH = {Imm, R0[3:0]};
  assign movL = {R0[7:4], Imm};
endmodule

module control (
  input  [3:0] LdStMov,
  input  [3:0] BrJump,
  input  [3:0] ULA1,
  input  [3:0] ULA2,
  output High,
  output Move,
  output WELdStMov,
  output WEmem,
  output brzr,
  output RBrJump,
  output jump,
  output IBrJump,
  output WEULA1,
  output [2:0] opULA1,
  output WEULA2,
  output [2:0] opoULA2
);

  wire and_4_out, nand_1_out, nand_2_out, nand_3_out, not_1_out, not_2_out, not_3_out;

  not not_1 (not_1_out, BrJump[1]);
  not not_2 (not_2_out, BrJump[0]);
  nand nand_1 (nand_1_out, ULA1[0], ULA1[1], ULA1[2]);
  nand nand_2 (nand_2_out, ULA2[0], ULA2[1], ULA2[2]);
  nor nor_1 (brzr, BrJump[0], BrJump[1], BrJump[2], BrJump[3]);
  nor nor_2 (jump, BrJump[0], not_1_out, BrJump[2], BrJump[3]);
  nor nor_3 (IBrJump, not_2_out, BrJump[1], BrJump[2], BrJump[3]);
  and and_1 (WEULA1, nand_1_out, ULA1[3]);
  Multiplexer #(.width(3)) multiplexer_1 (.in0(3'b000), .in1(ULA1[2:0]), .out(opULA1), .sel(WEULA1));
  and and_2 (WEULA2, nand_2_out, ULA2[3]);
  Multiplexer #(.width(3)) multiplexer_2 (.in0(3'b000), .in1(ULA2[2:0]), .out(opoULA2), .sel(WEULA2));
  and and_3 (High, ~LdStMov[0], LdStMov[1], LdStMov[2], ~LdStMov[3]);  // AND_Gate
  and and_4 (and_4_out, LdStMov[0], LdStMov[1], LdStMov[2], ~LdStMov[3]);  // AND_Gate
  nand nand_3 (nand_3_out, LdStMov[0], ~LdStMov[1], LdStMov[2], ~LdStMov[3]);  // NAND_Gate
  not not_3 (not_3_out, LdStMov[3]);
  and and_5 (WEmem, LdStMov[0], ~LdStMov[1], LdStMov[2], ~LdStMov[3]);  // AND_Gate
  or or_1 (RBrJump, brzr, jump);
  or or_2 (Move, High, and_4_out);
  and and_6 (WELdStMov, nand_3_out, LdStMov[2], not_3_out);
endmodule
